# Fritzing sketch DHT11LCDSWLED (saved by Fritzing 0.9.3b)
breadboards: 1

parts:
  부품1 = Arduino Uno (Rev3)
  DHT11 = Humidity and Temperature Sensor DHT11
  LCD1 = LCD screen
  R1 = Rotary Potentiometer (Small) [maximum_resistance=100kΩ package=THT]
  S1 = Pushbutton [package="[THT]"]

nets:
  N1: 부품1.D8, DHT11.Data-signal
  N2: 부품1.D11_PWM/MOSI, LCD1.E
  N3: 부품1.D12/MISO, LCD1.RS
  N4: 부품1.D2, LCD1.DB7
  N5: 부품1.D3_PWM, LCD1.DB6
  N6: 부품1.D4, LCD1.DB5
  N7: 부품1.D5_PWM, LCD1.DB4
  5V: 부품1.5V, DHT11.Vcc, LCD1.VDD, LCD1.LED+, R1.leg2
  GND: 부품1.GND, DHT11.GND_1, LCD1.VSS, LCD1.R/W, R1.leg1, S1.Pin_1, S1.Pin_2
  N8: LCD1.V0, R1.wiper
  N9: LCD1.LED-, S1.Pin_3, S1.Pin_4

custom parts:
  Humidity and Temperature Sensor DHT11: Digital relative humidity & temperature sensor DHT11
