# Fritzing sketch DHT11Only (saved by Fritzing 0.9.3b)
breadboards: 1

parts:
  부품1 = Arduino Uno (Rev3)
  DHT1 = Humidity and Temperature Sensor DHT11

nets:
  N1: 부품1.D8, DHT1.Data-signal
  N2: 부품1.GND, DHT1.GND_1
  5V: 부품1.5V, DHT1.Vcc

custom parts:
  Humidity and Temperature Sensor DHT11: Digital relative humidity & temperature sensor DHT11
